// Digital circuit CPU.dig as structural Verilog
module CPU (
  input  clk,
  input  CLR_PC
);

  wire comparator_1_eq, comparator_2_eq, comparator_3_eq, comparator_4_eq, flash_memory_1_p2,
       programme_counter_1_p2, programme_counter_1_p7;
  wire [7:0] flash_memory_1_p4, programme_counter_1_p1;

  Comparator #(.Bits(8)) comparator_1 (.a(flash_memory_1_p4), .b(8'h1), .eq(comparator_1_eq));  // open: gt, lt
  Comparator #(.Bits(8)) comparator_2 (.a(flash_memory_1_p4), .b(8'h2), .eq(comparator_2_eq));  // open: gt, lt
  Comparator #(.Bits(8)) comparator_3 (.a(flash_memory_1_p4), .b(8'h5), .eq(comparator_3_eq));  // open: gt, lt
  Comparator #(.Bits(8)) comparator_4 (.a(flash_memory_1_p4), .b(8'h6), .eq(comparator_4_eq));  // open: gt, lt
  // Programme_Counter programme_counter_1: pin names not known; wires that end beside it: programme_counter_1_p1, programme_counter_1_p2, clk, comparator_1_eq, comparator_2_eq, CLR_PC, programme_counter_1_p7
  // Flash_Memory flash_memory_1: pin names not known; wires that end beside it: programme_counter_1_p7, flash_memory_1_p2, clk, flash_memory_1_p4, programme_counter_1_p1, programme_counter_1_p2
  ALU alu_1 (
    .CMD(flash_memory_1_p4), .DAT(programme_counter_1_p1), .CLK(clk), .Q(programme_counter_1_p1),
    .DAT_dis(flash_memory_1_p2));
  // RAM ram_1: pin names not known; wires that end beside it: programme_counter_1_p1, programme_counter_1_p2, comparator_3_eq, comparator_4_eq, clk, programme_counter_1_p1, programme_counter_1_p7, flash_memory_1_p4, programme_counter_1_p1, programme_counter_1_p2

  // Notes on the sheet:
  //   clk: Hz: 5
  //   LN
  //   CMD
  //   LN: output from the programmme counter,
  //   the current line of code being executed
  //   DAT
  //   ADR
  //   CLK
  //   commands where a bus needs to be disabled for 2 cycles:
  //   Storage: 
  //   - load > data
  //   ALU:
  //   - add > data
  //   - add with carry > data
  //   - subtract > data
  //   incrementor:
  //   - increment > data
  //   - decrement > data
  //   logic:
  //   - binary not
  //   - binary or
  //   - binary and
  //   - binary xor
  //   - bitwise not
  //   - bitwise or
  //   - bitwise and
  //   - bitwise xor
  //   a/b/c registers:
  //   - load a > data
  //   - load b > data
  //   - load c > data
  //   compare:
  //   - bigger > data
  //   - equal > data
  //   - smaller > data
  //   flag reg:
  //   - load carry > data
  //   - load overflow > data
  //   - load flags > data
endmodule
